// Logisim project homework2.circ as structural Verilog: 4 circuits, main circuit vote
module vote (
  input  judge,
  input  member1,
  input  member2,
  input  member3,
  input  member4,
  output ou1,
  output ou2,
  output ou3,
  output ou4
);

  wire clk, clock_1_out, nQ1, nQ2, nQ3, nQ4;

  Clock clock_1 (.out(clock_1_out));
  D_Flip_Flop d_ff_1 (.clk(clk), .D(member1), .Q(ou1), .Qn(nQ1), .reset(judge));  // open: preset, en
  D_Flip_Flop d_ff_2 (.clk(clk), .D(member2), .Q(ou2), .Qn(nQ2), .reset(judge));  // open: preset, en
  D_Flip_Flop d_ff_3 (.clk(clk), .D(member3), .Q(ou3), .Qn(nQ3), .reset(judge));  // open: preset, en
  D_Flip_Flop d_ff_4 (.clk(clk), .D(member4), .Q(ou4), .Qn(nQ4), .reset(judge));  // open: preset, en
  nand nand_1 (clk, nQ1, nQ2, nQ3, nQ4, clock_1_out);

  // Other names for the same wires on the sheet: reset = judge
endmodule

module shop (
  input  money,
  input  commodity,
  output res
);

  wire clock_1_out;
  wire [1:0] change_for_shop_1_next0, now;

  change_for_shop change_for_shop_1 (
    .in(money), .state1(now[1]), .state0(now[0]), .next1(change_for_shop_1_next0[1]),
    .next0(change_for_shop_1_next0[0]));
  Clock clock_1 (.out(clock_1_out));
  change_for_print change_for_print_1 (.in(money), .state1(now[1]), .state0(now[0]), .out(commodity), .res(res));
  Register #(.width(2)) register_1 (.D(change_for_shop_1_next0), .Q(now), .clk(clock_1_out));  // open: en, clr

  // Notes on the sheet:
  //   输入0为5分钱，输入1为一角钱
  //   输出0为找零0元，输入1为找零5分钱
endmodule

module change_for_shop (
  input  in,
  input  state1,
  input  state0,
  output next1,
  output next0
);

  wire not_1_out, not_2_out;

  or or_1 (next1, state0, state1, in);
  not not_1 (not_1_out, in);
  not not_2 (not_2_out, state0);
  and and_1 (next0, not_1_out, not_2_out);
endmodule

module change_for_print (
  input  in,
  input  state1,
  input  state0,
  output out,
  output res
);

  wire and_1_out, and_2_out;

  and and_1 (and_1_out, state1, state0);
  and and_2 (and_2_out, in, state1);
  and and_3 (res, in, state1, state0);
  or or_1 (out, and_1_out, and_2_out);
endmodule
