// Logisim project homework3.circ as structural Verilog: 1 circuit, main circuit main
module main (
);

  wire undriven, undriven_2, undriven_3, undriven_4, undriven_5, undriven_6, undriven_7, undriven_8;
  wire [7:0] register_1_q, register_2_q, register_17_q, register_25_q, register_26_q, register_41_q,
       register_42_q, register_57_q;

  Register register_1 (.Q(register_1_q), .clk(undriven));  // open: D, en, clr
  Register register_2 (.Q(register_2_q), .clk(undriven));  // open: D, en, clr
  Register register_3 (.Q(register_1_q), .clk(undriven_4));  // open: D, en, clr
  Register register_4 (.Q(register_2_q), .clk(undriven_4));  // open: D, en, clr
  Register register_5 (.Q(register_1_q), .clk(undriven_7));  // open: D, en, clr
  Register register_6 (.Q(register_2_q), .clk(undriven_7));  // open: D, en, clr
  Register register_7 (.Q(register_1_q), .clk(undriven_3));  // open: D, en, clr
  Register register_8 (.Q(register_2_q), .clk(undriven_3));  // open: D, en, clr
  Register register_9 (.Q(register_2_q), .clk(undriven_2));  // open: D, en, clr
  Register register_10 (.Q(register_1_q), .clk(undriven_2));  // open: D, en, clr
  Register register_11 (.Q(register_2_q), .clk(undriven_5));  // open: D, en, clr
  Register register_12 (.Q(register_1_q), .clk(undriven_5));  // open: D, en, clr
  Register register_13 (.Q(register_1_q), .clk(undriven_8));  // open: D, en, clr
  Register register_14 (.Q(register_2_q), .clk(undriven_8));  // open: D, en, clr
  Register register_15 (.Q(register_2_q), .clk(undriven_6));  // open: D, en, clr
  Register register_16 (.Q(register_1_q), .clk(undriven_6));  // open: D, en, clr
  Register register_17 (.Q(register_17_q), .clk(undriven));  // open: D, en, clr
  Register register_18 (.Q(register_17_q), .clk(undriven_4));  // open: D, en, clr
  Register register_19 (.Q(register_17_q), .clk(undriven_7));  // open: D, en, clr
  Register register_20 (.Q(register_17_q), .clk(undriven_3));  // open: D, en, clr
  Register register_21 (.Q(register_17_q), .clk(undriven_2));  // open: D, en, clr
  Register register_22 (.Q(register_17_q), .clk(undriven_5));  // open: D, en, clr
  Register register_23 (.Q(register_17_q), .clk(undriven_8));  // open: D, en, clr
  Register register_24 (.Q(register_17_q), .clk(undriven_6));  // open: D, en, clr
  Register register_25 (.Q(register_25_q), .clk(undriven));  // open: D, en, clr
  Register register_26 (.Q(register_26_q), .clk(undriven));  // open: D, en, clr
  Register register_27 (.Q(register_26_q), .clk(undriven_4));  // open: D, en, clr
  Register register_28 (.Q(register_25_q), .clk(undriven_4));  // open: D, en, clr
  Register register_29 (.Q(register_25_q), .clk(undriven_7));  // open: D, en, clr
  Register register_30 (.Q(register_26_q), .clk(undriven_7));  // open: D, en, clr
  Register register_31 (.Q(register_26_q), .clk(undriven_3));  // open: D, en, clr
  Register register_32 (.Q(register_25_q), .clk(undriven_3));  // open: D, en, clr
  Register register_33 (.Q(register_25_q), .clk(undriven_2));  // open: D, en, clr
  Register register_34 (.Q(register_26_q), .clk(undriven_2));  // open: D, en, clr
  Register register_35 (.Q(register_25_q), .clk(undriven_5));  // open: D, en, clr
  Register register_36 (.Q(register_26_q), .clk(undriven_5));  // open: D, en, clr
  Register register_37 (.Q(register_26_q), .clk(undriven_8));  // open: D, en, clr
  Register register_38 (.Q(register_25_q), .clk(undriven_8));  // open: D, en, clr
  Register register_39 (.Q(register_26_q), .clk(undriven_6));  // open: D, en, clr
  Register register_40 (.Q(register_25_q), .clk(undriven_6));  // open: D, en, clr
  Register register_41 (.Q(register_41_q), .clk(undriven));  // open: D, en, clr
  Register register_42 (.Q(register_42_q), .clk(undriven));  // open: D, en, clr
  Register register_43 (.Q(register_42_q), .clk(undriven_4));  // open: D, en, clr
  Register register_44 (.Q(register_41_q), .clk(undriven_4));  // open: D, en, clr
  Register register_45 (.Q(register_41_q), .clk(undriven_7));  // open: D, en, clr
  Register register_46 (.Q(register_42_q), .clk(undriven_7));  // open: D, en, clr
  Register register_47 (.Q(register_41_q), .clk(undriven_3));  // open: D, en, clr
  Register register_48 (.Q(register_42_q), .clk(undriven_3));  // open: D, en, clr
  Register register_49 (.Q(register_41_q), .clk(undriven_2));  // open: D, en, clr
  Register register_50 (.Q(register_42_q), .clk(undriven_2));  // open: D, en, clr
  Register register_51 (.Q(register_41_q), .clk(undriven_5));  // open: D, en, clr
  Register register_52 (.Q(register_42_q), .clk(undriven_5));  // open: D, en, clr
  Register register_53 (.Q(register_42_q), .clk(undriven_8));  // open: D, en, clr
  Register register_54 (.Q(register_41_q), .clk(undriven_8));  // open: D, en, clr
  Register register_55 (.Q(register_42_q), .clk(undriven_6));  // open: D, en, clr
  Register register_56 (.Q(register_41_q), .clk(undriven_6));  // open: D, en, clr
  Register register_57 (.Q(register_57_q), .clk(undriven));  // open: D, en, clr
  Register register_58 (.Q(register_57_q), .clk(undriven_4));  // open: D, en, clr
  Register register_59 (.Q(register_57_q), .clk(undriven_7));  // open: D, en, clr
  Register register_60 (.Q(register_57_q), .clk(undriven_3));  // open: D, en, clr
  Register register_61 (.Q(register_57_q), .clk(undriven_2));  // open: D, en, clr
  Register register_62 (.Q(register_57_q), .clk(undriven_5));  // open: D, en, clr
  Register register_63 (.Q(register_57_q), .clk(undriven_8));  // open: D, en, clr
  Register register_64 (.Q(register_57_q), .clk(undriven_6));  // open: D, en, clr
endmodule
