// Logisim project homework4.circ as structural Verilog: 3 circuits, main circuit main
module main (
);

  wire cpu_1_out_5, cpu_1_out_6, cpu_1_out_8, cpu_1_out_10, cpu_1_out_11, cpu_1_out_21, \n74138译码器_1_out_11 ,
       \n74138译码器_1_out_12 , \n74138译码器_1_out_13 , \n74138译码器_1_out_14 ;
  wire [2:0] cpu_1_out_19, cpu_1_out_26;
  wire [4:3] cpu_1_out_4;
  wire [11:0] Address;

  CPU cpu_1 (
    .out_5(cpu_1_out_5), .out_7(Address[3]), .out_9(Address[4]), .out_11(cpu_1_out_11), .out_13(Address[9]),
    .out_19(cpu_1_out_19[0]), .out_20(cpu_1_out_4[4]), .out_21(cpu_1_out_21), .out_16(Address[8]),
    .out_6(cpu_1_out_6), .out_8(cpu_1_out_8), .out_10(cpu_1_out_10), .out_12(Address[11]),
    .out_14(Address[7]), .out_18(Address[6]), .out_22(Address[5]), .out_23(cpu_1_out_19[1]),
    .out_24(cpu_1_out_26[0]), .out_25(cpu_1_out_26[1]), .out_26(cpu_1_out_26[2]), .out_1(Address[10]),
    .out_2(Address[2]), .out_3(cpu_1_out_19[2]), .out_4(cpu_1_out_4[3]), .out_15(Address[1]),
    .out_17(Address[0]));
  \_74138译码器  \u_74138译码器_1  (
    .in_4(cpu_1_out_6), .in_5(cpu_1_out_10), .in_6(cpu_1_out_11), .in_3(1'b1), .in_2(cpu_1_out_5),
    .in_1(cpu_1_out_8), .out_11(\n74138译码器_1_out_11 ), .out_12(\n74138译码器_1_out_12 ),
    .out_13(\n74138译码器_1_out_13 ), .out_14(\n74138译码器_1_out_14 ));  // open: out_7, out_8, out_9, out_10
  ROM #(.addrWidth(12), .dataWidth(3)) rom_1 (.addr(Address), .data(cpu_1_out_26));  // open: sel
  ROM #(.addrWidth(12), .dataWidth(3)) rom_2 (.addr(Address), .data(cpu_1_out_19));  // open: sel
  RAM #(.addrWidth(12)) ram_1 (
    .addr(Address), .data({{2{cpu_1_out_26[1]}}, cpu_1_out_26[0], cpu_1_out_4, cpu_1_out_19}),
    .sel(cpu_1_out_21));  // open: clk, ld, clr
  RAM #(.addrWidth(12)) ram_2 (
    .addr(Address), .data({{2{cpu_1_out_26[1]}}, cpu_1_out_26[0], cpu_1_out_4, cpu_1_out_19}),
    .sel(cpu_1_out_21));  // open: clk, ld, clr
  RAM #(.addrWidth(12)) ram_3 (
    .addr(Address), .data({{2{cpu_1_out_26[1]}}, cpu_1_out_26[0], cpu_1_out_4, cpu_1_out_19}),
    .sel(cpu_1_out_21));  // open: clk, ld, clr
endmodule

module CPU (
  output out_1,
  output out_2,
  output out_3,
  output out_4,
  output out_5,
  output out_6,
  output out_7,
  output out_8,
  output out_9,
  output out_10,
  output out_11,
  output out_12,
  output out_13,
  output out_14,
  output out_15,
  output out_16,
  output out_17,
  output out_18,
  output out_19,
  output out_20,
  output out_21,
  output out_22,
  output out_23,
  output out_24,
  output out_25,
  output out_26
);
endmodule

module \_74138译码器  (
  input  in_1,
  input  in_2,
  input  in_3,
  input  in_4,
  input  in_5,
  input  in_6,
  output out_7,
  output out_8,
  output out_9,
  output out_10,
  output out_11,
  output out_12,
  output out_13,
  output out_14
);
endmodule
