// Logisim project 2021_p0_1.circ as structural Verilog: 2 circuits, main circuit main
module main (
  input  [1:0] boss,
  input  [1:0] member1,
  input  [1:0] member2,
  input  [1:0] member3,
  output out
);

  wire calc_1_deny, calc_1_lose, calc_1_win, calc_2_lose, calc_2_win, calc_3_lose, calc_3_win, calc_4_lose,
       calc_4_win, comparator_1_gt, not_1_out;
  wire [3:0] adder_1_out, adder_2_out, adder_3_out, adder_4_out, adder_5_out, adder_6_out,
       bit_extender_1_out, bit_extender_2_out, bit_extender_3_out, bit_extender_4_out, bit_extender_5_out,
       bit_extender_6_out, bit_extender_7_out, bit_extender_8_out;

  calc calc_1 (.choose(boss[1]), .en(boss[0]), .deny(calc_1_deny), .win(calc_1_win), .lose(calc_1_lose));
  calc calc_2 (.choose(member1[1]), .en(member1[0]), .win(calc_2_win), .lose(calc_2_lose));  // open: deny
  calc calc_3 (.choose(member2[1]), .en(member2[0]), .win(calc_3_win), .lose(calc_3_lose));  // open: deny
  calc calc_4 (.choose(member3[1]), .en(member3[0]), .win(calc_4_win), .lose(calc_4_lose));  // open: deny
  assign bit_extender_1_out = {{3{1'b0}}, calc_1_win};  // Bit_Extender bit_extender_1
  assign bit_extender_2_out = {{3{1'b0}}, calc_1_lose};  // Bit_Extender bit_extender_2
  assign bit_extender_3_out = {{3{1'b0}}, calc_2_win};  // Bit_Extender bit_extender_3
  assign bit_extender_4_out = {{3{1'b0}}, calc_2_lose};  // Bit_Extender bit_extender_4
  assign bit_extender_5_out = {{3{1'b0}}, calc_3_win};  // Bit_Extender bit_extender_5
  assign bit_extender_6_out = {{3{1'b0}}, calc_3_lose};  // Bit_Extender bit_extender_6
  assign bit_extender_7_out = {{3{1'b0}}, calc_4_win};  // Bit_Extender bit_extender_7
  assign bit_extender_8_out = {{3{1'b0}}, calc_4_lose};  // Bit_Extender bit_extender_8
  Adder #(.width(4)) adder_1 (.a(bit_extender_3_out), .b(bit_extender_5_out), .out(adder_1_out));  // open: cin, cout
  Adder #(.width(4)) adder_2 (.a(bit_extender_4_out), .b(bit_extender_6_out), .out(adder_2_out));  // open: cin, cout
  Adder #(.width(4)) adder_3 (.a(adder_1_out), .b(bit_extender_7_out), .out(adder_3_out));  // open: cin, cout
  Adder #(.width(4)) adder_4 (.a(adder_2_out), .b(bit_extender_8_out), .out(adder_4_out));  // open: cin, cout
  Adder #(.width(4)) adder_5 (.a(bit_extender_1_out), .b(adder_3_out), .out(adder_5_out));  // open: cin, cout
  Adder #(.width(4)) adder_6 (.a(bit_extender_2_out), .b(adder_4_out), .out(adder_6_out));  // open: cin, cout
  not not_1 (not_1_out, calc_1_deny);
  Comparator #(.width(4), .mode("unsigned")) comparator_1 (
    .a(adder_5_out), .b(adder_6_out), .gt(comparator_1_gt));  // open: eq, lt
  and and_1 (out, not_1_out, comparator_1_gt);
endmodule

module calc (
  input  choose,
  input  en,
  output deny,
  output win,
  output lose
);

  wire demultiplexer_1_out0, demultiplexer_1_out1, not_1_out, not_2_out;

  Demultiplexer demultiplexer_1 (
    .out0(demultiplexer_1_out0), .out1(demultiplexer_1_out1), .in(1'b1), .sel(choose));  // open: en
  and and_1 (win, demultiplexer_1_out0, not_1_out);
  not not_1 (not_1_out, en);
  and and_2 (lose, demultiplexer_1_out1, not_2_out);
  not not_2 (not_2_out, en);
  and and_3 (deny, choose, en);
endmodule
