// Logisim project 2021_p0_2.circ as structural Verilog: 3 circuits, main circuit main
module main (
  input  [1:0] in,
  input  reset,
  output [1:0] out
);

  wire clock_1_out;
  wire [2:0] change_1_next0, next;

  change change_1 (
    .state2(next[2]), .state1(next[1]), .state0(next[0]), .in1(in[1]), .in0(in[0]),
    .next2(change_1_next0[2]), .next1(change_1_next0[1]), .next0(change_1_next0[0]));
  Clock clock_1 (.out(clock_1_out));
  Register #(.width(3)) register_1 (.D(change_1_next0), .Q(next), .clk(clock_1_out), .clr(reset));  // open: en
  print print_1 (
    .state2(next[2]), .state1(next[1]), .state0(next[0]), .in2(in[1]), .in1(in[0]), .out2(out[1]),
    .out1(out[0]));
endmodule

module change (
  input  state2,
  input  state1,
  input  state0,
  input  in1,
  input  in0,
  output next2,
  output next1,
  output next0
);

  wire and_2_out, and_3_out, and_4_out, and_5_out, and_6_out, not_1_out, not_2_out, not_3_out, not_4_out,
       not_5_out, not_6_out, not_7_out;

  not not_1 (not_1_out, state0);
  not not_2 (not_2_out, state1);
  not not_3 (not_3_out, in1);
  not not_4 (not_4_out, in0);
  not not_5 (not_5_out, state0);
  not not_6 (not_6_out, state1);
  not not_7 (not_7_out, state0);
  and and_1 (next2, state1, not_1_out, in1);
  and and_2 (and_2_out, not_2_out, state0, not_3_out, not_4_out);
  and and_3 (and_3_out, state1, not_5_out, in0);
  and and_4 (and_4_out, not_6_out, in1);
  and and_5 (and_5_out, state0, in1);
  and and_6 (and_6_out, state1, not_7_out, in0);
  or or_1 (next1, and_2_out, and_3_out);
  or or_2 (next0, and_4_out, and_5_out, and_6_out);
endmodule

module print (
  input  state2,
  input  state1,
  input  state0,
  input  in2,
  input  in1,
  output out2,
  output out1
);

  and and_1 (out2, state2, in1);
  and and_2 (out1, state1, state0, in1);
endmodule
