// Logisim project 2021_p0_3.circ as structural Verilog: 2 circuits, main circuit main
// Nth
module main (
  input  [4:0] in,
  output [31:0] Nth
);

  wire clk, comparator_1_lt, counter_1_q, counter_2_q, counter_3_q, counter_4_out_3, en;
  wire [1:0] bit_extender_1_out;
  wire [2:0] bit_extender_2_out, multiplexer_4_out;
  wire [4:0] in_sub;
  wire [31:0] multiplexer_1_out, multiplexer_2_out, multiplexer_3_out, out, S_n, S_n_1, S_n_2, S_n_3;

  Clock clock_1 (.out(clk));
  Multiplexer #(.width(32), .enable("false")) multiplexer_1 (
    .in0(32'h1), .in1(S_n_2), .out(multiplexer_1_out), .sel(counter_1_q));
  Counter #(.width(1), .max('h1), .ongoal("stay")) counter_1 (
    .Q(counter_1_q), .clk(clk));  // open: load, D, count, carry, clr
  Multiplexer #(.width(32), .enable("false")) multiplexer_2 (
    .in0(32'h1), .in1(S_n_1), .out(multiplexer_2_out), .sel(counter_2_q));
  Counter #(.width(1), .max('h1), .ongoal("stay")) counter_2 (
    .Q(counter_2_q), .clk(clk));  // open: load, D, count, carry, clr
  Multiplexer #(.width(32), .enable("false")) multiplexer_3 (
    .in0(32'h1), .in1(S_n), .out(multiplexer_3_out), .sel(counter_3_q));
  Counter #(.width(1), .max('h1), .ongoal("stay")) counter_3 (
    .Q(counter_3_q), .clk(clk));  // open: load, D, count, carry, clr
  // Probe on S_n_3
  Subtractor #(.width(5)) subtractor_1 (.a(in), .b(5'b00100), .out(in_sub));  // open: bin, bout
  counter counter_4 (.in(in_sub), .clk(clk), .out_3(counter_4_out_3));
  // Probe on S_n_2
  not not_1 (en, counter_4_out_3);
  Register #(.width(32)) register_1 (.D(multiplexer_1_out), .en(en), .Q(S_n_3), .clk(clk));  // open: clr
  Register #(.width(32)) register_2 (.D(multiplexer_2_out), .en(en), .Q(S_n_2), .clk(clk));  // open: clr
  Register #(.width(32)) register_3 (.D(multiplexer_3_out), .en(en), .Q(S_n_1), .clk(clk));  // open: clr
  // Probe on S_n_1
  Bit_Extender #(.in_width(5), .out_width(2)) bit_extender_1 (.in(in), .out(bit_extender_1_out));
  Comparator #(.width(5), .mode("unsigned")) comparator_1 (.a(in), .b(5'b00100), .lt(comparator_1_lt));  // open: gt, eq
  // Probe on out
  Adder #(.width(32)) adder_1 (.a(S_n_1), .b(out), .out(S_n));  // open: cin, cout
  // Probe on S_n
  Multiplexer #(.width(3)) multiplexer_4 (
    .in0(3'b100), .in1(bit_extender_2_out), .out(multiplexer_4_out), .sel(comparator_1_lt));  // open: en
  assign bit_extender_2_out = {{1{1'b0}}, bit_extender_1_out};  // Bit_Extender bit_extender_2
  assign out = S_n_2 & S_n_3;  // AND_Gate and_1, 32 bits wide
  Multiplexer #(.select(3), .width(32)) multiplexer_5 (
    .in0({32{1'b0}}), .in1(32'h1), .in2(32'h1), .in3(32'h1), .in4(S_n), .out(Nth), .sel(multiplexer_4_out));  // open: in5, in6, in7, en
endmodule

module counter (
  input  [4:0] in,
  input  clk,
  output out_3
);

  wire [4:0] counter_1_q;

  Counter #(.width(5), .max('h1f), .ongoal("stay")) counter_1 (
    .Q(counter_1_q), .clk(clk));  // open: load, D, count, carry, clr
  Comparator #(.width(5), .mode("unsigned")) comparator_1 (.a(in), .b(counter_1_q), .lt(out_3));  // open: gt, eq
endmodule
