// Logisim project CRC.circ as structural Verilog: 2 circuits, main circuit CRC
module CRC (
  input  [7:0] A,
  input  [3:0] B,
  output [10:0] out_3
);

  wire [2:0] mod_1_out_4, mod_2_out_4, mod_3_out_4, mod_4_out_4, mod_5_out_4, mod_6_out_4, mod_7_out_4;
  wire [10:0] bit_extender_1_out, shifter_1_out;

  assign bit_extender_1_out = {{3{1'b0}}, A};  // Bit_Extender bit_extender_1
  Shifter #(.width(11)) shifter_1 (.in(bit_extender_1_out), .\dist (4'b0011), .out(shifter_1_out));
  mod mod_1 (.A(shifter_1_out[10:8]), .Cin(shifter_1_out[7]), .B(B), .out_4(mod_1_out_4));
  mod mod_2 (.A(mod_1_out_4), .Cin(shifter_1_out[6]), .B(B), .out_4(mod_2_out_4));
  mod mod_3 (.A(mod_2_out_4), .Cin(shifter_1_out[5]), .B(B), .out_4(mod_3_out_4));
  mod mod_4 (.A(mod_3_out_4), .Cin(shifter_1_out[4]), .B(B), .out_4(mod_4_out_4));
  mod mod_5 (.A(mod_4_out_4), .Cin(shifter_1_out[3]), .B(B), .out_4(mod_5_out_4));
  mod mod_6 (.A(mod_5_out_4), .Cin(shifter_1_out[2]), .B(B), .out_4(mod_6_out_4));
  mod mod_7 (.A(mod_6_out_4), .Cin(shifter_1_out[1]), .B(B), .out_4(mod_7_out_4));
  mod mod_8 (.A(mod_7_out_4), .Cin(shifter_1_out[0]), .B(B), .out_4(out_3[2:0]));

  assign out_3[10:3] = A;
endmodule

module mod (
  input  [2:0] A,
  input  Cin,
  input  [3:0] B,
  output [2:0] out_4
);

  wire [3:0] multiplexer_1_out, xor_1_out;

  assign xor_1_out = {A, Cin} ^ B;  // XOR_Gate xor_1, 4 bits wide
  Multiplexer #(.width(4)) multiplexer_1 (
    .in0({A, Cin}), .in1(xor_1_out), .out(multiplexer_1_out), .sel(A[2]));  // open: en
  Bit_Extender #(.in_width(4), .out_width(3)) bit_extender_1 (.in(multiplexer_1_out), .out(out_4));

  // Other names for the same wires on the sheet: A_t[3:0] = {A, Cin}; choose = A[2]
endmodule
