// Logisim project fsm.circ as structural Verilog: 4 circuits, main circuit fsm
module fsm (
  input  clr,
  input  [1:0] in,
  output z
);

  wire clock_1_out;
  wire [1:0] change_1_next0, multiplexer_1_out, register_1_q;

  Clock clock_1 (.out(clock_1_out));
  // Probe on in
  change change_1 (
    .in1(in[1]), .in0(in[0]), .state1(register_1_q[1]), .state0(register_1_q[0]), .next1(change_1_next0[1]),
    .next0(change_1_next0[0]));
  Register #(.width(2)) register_1 (.D(multiplexer_1_out), .Q(register_1_q), .clk(clock_1_out));  // open: en, clr
  Multiplexer #(.width(2)) multiplexer_1 (
    .in0(change_1_next0), .in1(2'b00), .out(multiplexer_1_out), .sel(clr));  // open: en
  // Probe on register_1_q
  // Probe on in
  print print_1 (.in1(in[1]), .in0(in[0]), .next1(register_1_q[1]), .next0(register_1_q[0]), .z(z));
endmodule

module change (
  input  in1,
  input  in0,
  input  state1,
  input  state0,
  output next1,
  output next0
);

  wire and_1_out, and_2_out, and_3_out, and_4_out, and_5_out, and_6_out, and_7_out, not_1_out, not_2_out,
       not_3_out, not_4_out, not_5_out, not_6_out, not_7_out, not_8_out, not_9_out, not_10_out, not_11_out,
       not_12_out, not_13_out;

  not not_1 (not_1_out, in1);
  and and_1 (and_1_out, not_1_out, not_2_out, state0);
  not not_2 (not_2_out, state1);
  not not_3 (not_3_out, in0);
  not not_4 (not_4_out, state1);
  and and_2 (and_2_out, not_3_out, not_4_out, state0);
  not not_5 (not_5_out, in0);
  and and_3 (and_3_out, not_5_out, state1, not_6_out);
  not not_6 (not_6_out, state0);
  not not_7 (not_7_out, in0);
  not not_8 (not_8_out, state1);
  and and_4 (and_4_out, not_7_out, not_8_out, state0);
  not not_9 (not_9_out, in0);
  and and_5 (and_5_out, not_9_out, state1, not_10_out);
  not not_10 (not_10_out, state0);
  not not_11 (not_11_out, in1);
  and and_6 (and_6_out, not_11_out, in0, not_12_out);
  not not_12 (not_12_out, state0);
  not not_13 (not_13_out, in1);
  and and_7 (and_7_out, not_13_out, in0, state1);
  or or_1 (next1, and_1_out, and_2_out, and_3_out);
  or or_2 (next0, and_4_out, and_5_out, and_6_out, and_7_out);
endmodule

module print (
  input  in1,
  input  in0,
  input  next1,
  input  next0,
  output z
);

  wire not_1_out;

  not not_1 (not_1_out, in0);
  and and_1 (z, not_1_out, next1, next0);
endmodule

module tb (
  input  in_1,
  output out_2,
  output halt
);

  wire clock_1_out;
  wire [2:0] ram_1_data;
  wire [7:0] counter_1_q;

  Clock clock_1 (.out(clock_1_out));
  Counter counter_1 (.Q(counter_1_q), .carry(halt), .clk(clock_1_out), .clr(in_1));  // open: load, D, count
  RAM #(.dataWidth(3)) ram_1 (.addr(counter_1_q), .data(ram_1_data));  // open: sel, clk, ld, clr
  // Probe on out_2
  // Probe on ram_1_data[2:1]
  fsm fsm_1 (.clr(ram_1_data[0]), .in(ram_1_data[2:1]), .z(out_2));
endmodule
