// Logisim project ftoi.circ as structural Verilog: 1 circuit, main circuit ftoi
module ftoi (
  input  [15:0] float,
  output [31:0] \int 
);

  wire choose, comparator_1_eq, comparator_2_eq, dir;
  wire [4:0] adder_1_out, bit_extender_3_out, not_1_out, num, subtractor_1_out;
  wire [10:0] demultiplexer_1_out0, demultiplexer_1_out1;
  wire [31:0] adder_2_out, bit_extender_1_out, bit_extender_2_out, multiplexer_1_out, not_2_out, out,
       shifter_1_out, shifter_2_out;

  Comparator #(.width(5), .mode("unsigned")) comparator_1 (
    .a(float[14:10]), .b({5{1'b1}}), .eq(comparator_1_eq));  // open: gt, lt
  Comparator #(.width(5), .mode("unsigned")) comparator_2 (
    .a(float[14:10]), .b({5{1'b0}}), .eq(comparator_2_eq));  // open: gt, lt
  Demultiplexer #(.width(11), .enable("false")) demultiplexer_1 (
    .out0(demultiplexer_1_out0), .out1(demultiplexer_1_out1), .in({1'b1, float[9:0]}), .sel(dir));
  // Probe on {1'b1, float[9:0]}
  // Probe on float[9:0]
  or or_1 (choose, comparator_1_eq, comparator_2_eq);
  // Probe on bit_extender_1_out
  assign bit_extender_1_out = {{21{1'b0}}, demultiplexer_1_out0};  // Bit_Extender bit_extender_1
  assign bit_extender_2_out = {{21{1'b0}}, demultiplexer_1_out1};  // Bit_Extender bit_extender_2
  Subtractor #(.width(5)) subtractor_1 (
    .a(float[14:10]), .b(5'b01111), .out(subtractor_1_out), .bout(dir));  // open: bin
  assign bit_extender_3_out = {{4{1'b0}}, dir};  // Bit_Extender bit_extender_3
  Shifter #(.width(32)) shifter_1 (.in(bit_extender_1_out), .\dist (num), .out(shifter_1_out));
  Shifter #(.width(32), .shift("lr")) shifter_2 (.in(bit_extender_2_out), .\dist (num), .out(shifter_2_out));
  assign not_1_out = ~subtractor_1_out;  // NOT_Gate not_1, 5 bits wide
  Adder #(.width(5)) adder_1 (.a(not_1_out), .b(bit_extender_3_out), .out(adder_1_out));  // open: cin, cout
  Multiplexer #(.width(32)) multiplexer_1 (
    .in0(shifter_1_out), .in1(shifter_2_out), .out(multiplexer_1_out), .sel(dir));  // open: en
  // Probe on multiplexer_1_out
  // Probe on num
  Multiplexer #(.width(5)) multiplexer_2 (.in0(subtractor_1_out), .in1(adder_1_out), .out(num), .sel(dir));  // open: en
  assign not_2_out = ~{{10{1'b0}}, multiplexer_1_out[31:10]};  // NOT_Gate not_2, 32 bits wide
  Adder #(.width(32)) adder_2 (.a(not_2_out), .b(32'h1), .out(adder_2_out));  // open: cin, cout
  Multiplexer #(.width(32)) multiplexer_3 (.in0(out), .in1({32{1'b0}}), .out(\int ), .sel(choose));  // open: en
  Multiplexer #(.width(32)) multiplexer_4 (
    .in0({{10{1'b0}}, multiplexer_1_out[31:10]}), .in1(adder_2_out), .out(out), .sel(float[15]));  // open: en

  // Other names for the same wires on the sheet: M[9:0] = float[9:0]; E[4:0] = float[14:10]; s = float[15]
endmodule
