// Logisim project navigation.circ as structural Verilog: 2 circuits, main circuit navigation
module navigation (
  input  [1:0] dir,
  input  clk,
  input  reset,
  output arrive,
  output hit
);

  wire change_hit, comparator_1_eq, counter_1_q;
  wire [2:0] change_next0, multiplexer_1_out, register_1_q;

  Multiplexer #(.width(3)) multiplexer_1 (
    .in0(register_1_q), .in1(3'b000), .out(multiplexer_1_out), .sel(comparator_1_eq));  // open: en
  Counter #(.width(1), .max('h1), .ongoal("stay")) counter_1 (
    .Q(counter_1_q), .clk(clk));  // open: load, D, count, carry, clr
  Comparator #(.width(1), .mode("unsigned")) comparator_1 (
    .a(counter_1_q), .b(1'b0), .eq(comparator_1_eq));  // open: gt, lt
  change change (
    .state2(multiplexer_1_out[2]), .state1(multiplexer_1_out[1]), .state0(multiplexer_1_out[0]),
    .dir1(dir[1]), .dir0(dir[0]), .next2(change_next0[2]), .next1(change_next0[1]), .next0(change_next0[0]),
    .hit(change_hit));
  // Probe on register_1_q
  Register #(.width(3)) register_1 (.D(change_next0), .Q(register_1_q), .clk(clk), .clr(reset));  // open: en
  Register #(.width(1)) register_2 (.D(change_hit), .Q(hit), .clk(clk), .clr(reset));  // open: en
  Comparator #(.width(3), .mode("unsigned")) comparator_2 (.a(register_1_q), .b(3'b100), .eq(arrive));  // open: gt, lt
endmodule

module change (
  input  state2,
  input  state1,
  input  state0,
  input  dir1,
  input  dir0,
  output next2,
  output next1,
  output next0,
  output hit
);

  wire and_1_out, and_2_out, and_3_out, and_4_out, and_5_out, and_6_out, and_7_out, and_8_out, and_9_out,
       and_10_out, and_11_out, and_12_out, and_13_out, and_14_out, and_15_out, and_16_out, and_17_out,
       and_18_out, and_19_out, and_20_out, and_21_out, and_22_out, and_23_out, and_24_out, and_25_out,
       and_26_out, and_27_out, not_1_out, not_2_out, not_3_out, not_4_out, not_5_out, not_6_out, not_7_out,
       not_8_out, not_9_out, not_10_out, not_11_out, not_12_out, not_13_out, not_14_out, not_15_out,
       not_16_out, not_17_out, not_18_out, not_19_out, not_20_out, not_21_out, not_22_out, not_23_out,
       not_24_out, not_25_out, not_26_out, not_27_out, not_28_out, not_29_out, not_30_out, not_31_out,
       not_32_out, not_33_out, not_34_out, not_35_out, not_36_out, not_37_out, not_38_out, not_39_out,
       not_40_out, not_41_out;

  not not_1 (not_1_out, state0);
  not not_2 (not_2_out, dir1);
  not not_3 (not_3_out, dir1);
  not not_4 (not_4_out, dir0);
  not not_5 (not_5_out, dir1);
  not not_6 (not_6_out, dir1);
  not not_7 (not_7_out, state1);
  not not_8 (not_8_out, dir1);
  not not_9 (not_9_out, dir1);
  not not_10 (not_10_out, state0);
  not not_11 (not_11_out, dir1);
  not not_12 (not_12_out, dir0);
  not not_13 (not_13_out, state0);
  not not_14 (not_14_out, dir0);
  not not_15 (not_15_out, state2);
  not not_16 (not_16_out, state1);
  not not_17 (not_17_out, state0);
  not not_18 (not_18_out, dir1);
  not not_19 (not_19_out, dir0);
  not not_20 (not_20_out, state2);
  not not_21 (not_21_out, dir0);
  not not_22 (not_22_out, state2);
  not not_23 (not_23_out, state1);
  not not_24 (not_24_out, state0);
  not not_25 (not_25_out, state2);
  not not_26 (not_26_out, state1);
  not not_27 (not_27_out, state0);
  not not_28 (not_28_out, state2);
  not not_29 (not_29_out, state1);
  not not_30 (not_30_out, state2);
  not not_31 (not_31_out, state0);
  not not_32 (not_32_out, state0);
  not not_33 (not_33_out, dir1);
  not not_34 (not_34_out, dir0);
  not not_35 (not_35_out, dir1);
  not not_36 (not_36_out, state2);
  not not_37 (not_37_out, dir0);
  not not_38 (not_38_out, dir1);
  not not_39 (not_39_out, state0);
  not not_40 (not_40_out, dir0);
  not not_41 (not_41_out, dir1);
  and and_1 (and_1_out, state1, not_1_out, not_2_out, dir0);
  and and_2 (and_2_out, state1, state0, not_3_out, not_4_out);
  and and_3 (and_3_out, state2, state0, not_5_out);
  and and_4 (and_4_out, state2, state1, not_6_out);
  and and_5 (and_5_out, not_7_out, state0, not_8_out);
  and and_6 (and_6_out, state0, not_9_out, dir0);
  and and_7 (and_7_out, state1, not_10_out, not_11_out, not_12_out);
  and and_8 (and_8_out, state1, not_13_out, dir1, dir0);
  and and_9 (and_9_out, state1, state0, dir1, not_14_out);
  and and_10 (and_10_out, state2, state0, dir1);
  and and_11 (and_11_out, state2, state1, dir1);
  and and_12 (and_12_out, not_15_out, not_16_out, not_17_out, not_18_out, not_19_out);
  and and_13 (and_13_out, state0, dir0);
  and and_14 (and_14_out, not_20_out, state1, dir1, not_21_out);
  and and_15 (and_15_out, state2, state0, dir1);
  and and_16 (and_16_out, state2, state1, dir1, dir0);
  and and_17 (and_17_out, not_22_out, not_23_out, not_24_out, dir0);
  and and_18 (and_18_out, not_25_out, not_26_out, not_27_out, dir1);
  and and_19 (and_19_out, not_28_out, not_29_out, dir1, dir0);
  and and_20 (and_20_out, not_30_out, not_31_out, dir1, dir0);
  and and_21 (and_21_out, state1, not_32_out, not_33_out, not_34_out);
  and and_22 (and_22_out, state1, state0, not_35_out, dir0);
  and and_23 (and_23_out, not_36_out, state1, state0, dir1, not_37_out);
  and and_24 (and_24_out, state2, state0, not_38_out);
  and and_25 (and_25_out, state2, state1, not_39_out, not_40_out);
  and and_26 (and_26_out, state2, state1, not_41_out);
  and and_27 (and_27_out, state2, state1, state0, dir0);
  or or_1 (next2, and_1_out, and_2_out, and_3_out, and_4_out);
  or or_2 (next1, and_5_out, and_6_out, and_7_out, and_8_out, and_9_out, and_10_out, and_11_out);
  or or_3 (next0, and_12_out, and_13_out, and_14_out, and_15_out, and_16_out);
  or or_4 (hit, and_17_out, and_18_out, and_19_out, and_20_out, and_21_out, and_22_out, and_23_out, and_24_out, and_25_out, and_26_out, and_27_out);
endmodule
