// Logisim project cpu.circ as structural Verilog: 8 circuits, main circuit main
module main (
  input  reset,
  output [31:0] Instr,
  output RegWrite,
  output [4:0] RegAddr,
  output [31:0] RegData,
  output MemWrite,
  output [4:0] MemAddr,
  output [31:0] MemData
);

  wire clk, eq, sign;
  wire [1:0] ALU_choose1, ALU_choose2, B_change, bit_extender_4_out, DM_type, \reg ;
  wire [2:0] ALUop, branch, choose;
  wire [31:0] bit_extender_1_out, bit_extender_2_out, bit_extender_3_out, imm32, multiplexer_1_out,
       multiplexer_2_out, multiplexer_3_out, PC, RD, RD1, res, shifter_1_out, shifter_2_out;

  Clock u_clk (.out(clk));
  // Probe on Instr[15:0]
  // Probe on imm32
  // Probe on Instr[31:26]
  // Probe on Instr[5:0]
  EXT ext_1 (.imm16(Instr[15:0]), .sign(sign), .imm32(imm32));
  assign bit_extender_1_out = {{6{1'b0}}, Instr[25:0]};  // Bit_Extender bit_extender_1
  Controller controller_1 (
    .op(Instr[31:26]), .func(Instr[5:0]), .ALUop(ALUop), .Wegrf(RegWrite), .WeDm(MemWrite), .branch(branch),
    .AluSrc1(ALU_choose1), .WhichReg(choose), .RegDst(\reg ), .SignExt(sign), .AluSrc2(ALU_choose2),
    .B_change(B_change), .DM_type(DM_type));
  Multiplexer #(.select(3), .width(32), .enable("false")) multiplexer_1 (
    .in0(imm32), .in1(imm32), .in2(bit_extender_1_out), .in3(RD1), .out(multiplexer_1_out), .sel(branch));  // open: in4, in5, in6, in7
  // Probe on multiplexer_1_out
  assign bit_extender_2_out = {{27{1'b0}}, Instr[10:6]};  // Bit_Extender bit_extender_2
  // Probe on Instr
  // Probe on Instr
  IFU ifu_1 (.branch(branch), .imm32(multiplexer_1_out), .instr(Instr), .clk(clk), .reset(reset), .PC(PC), .change(eq));
  // Probe on multiplexer_2_out
  Multiplexer #(.select(2), .width(32), .enable("false")) multiplexer_2 (
    .in0(RD1), .in1(MemData), .out(multiplexer_2_out), .sel(ALU_choose1));  // open: in2, in3
  Multiplexer #(.select(2), .width(32), .enable("false")) multiplexer_3 (
    .in0(MemData), .in1(imm32), .in2(bit_extender_2_out), .in3({32{1'b0}}), .out(multiplexer_3_out),
    .sel(ALU_choose2));
  // Probe on multiplexer_3_out
  ALU alu_1 (.A(multiplexer_2_out), .B(multiplexer_3_out), .change_2(eq), .res(res), .ALUop(ALUop), .change(B_change));
  // Probe on ALUop
  // Probe on Instr[31:26]
  // Probe on Instr[5:0]
  // Probe on Instr[15:0]
  // Probe on Instr[25:0]
  // Probe on res
  // Probe on Instr[25:21]
  // Probe on Instr[20:16]
  // Probe on Instr[15:11]
  // Probe on Instr[10:6]
  assign bit_extender_3_out = {{31{1'b0}}, eq};  // Bit_Extender bit_extender_3
  Shifter #(.width(32), .shift("lr")) shifter_1 (.in(res), .\dist (5'b00010), .out(shifter_1_out));
  Bit_Extender #(.in_width(32), .out_width(2)) bit_extender_4 (.in(res), .out(bit_extender_4_out));
  // Probe on \reg 
  Shifter #(.width(32)) shifter_2 (.in(imm32), .\dist (5'b10000), .out(shifter_2_out));
  // Probe on choose
  // Probe on MemAddr
  Bit_Extender #(.in_width(32), .out_width(5)) bit_extender_5 (.in(shifter_1_out), .out(MemAddr));
  // Probe on MemData
  // Probe on bit_extender_4_out
  // Probe on Instr[25:21]
  // Probe on Instr[20:16]
  // Probe on RegAddr
  Multiplexer #(.select(2), .width(5), .enable("false")) multiplexer_4 (
    .in0(Instr[15:11]), .in1(Instr[20:16]), .in2({5{1'b1}}), .out(RegAddr), .sel(\reg ));  // open: in3
  Multiplexer #(.select(3), .width(32), .enable("false")) multiplexer_5 (
    .in0(res), .in1(RD), .in2(shifter_2_out), .in3(PC), .in4(bit_extender_3_out), .out(RegData), .sel(choose));  // open: in5, in6, in7
  // Probe on RegData
  // Probe on RegData
  // Probe on RegData
  DM dm_1 (
    .Address(MemAddr), .clk(clk), .reset(reset), .WE(MemWrite), .DM_type(DM_type), .WD(MemData), .RD(RD),
    .low2(bit_extender_4_out));
  // Probe on RD1
  GRF grf_1 (
    .A1(Instr[25:21]), .A2(Instr[20:16]), .A3(RegAddr), .WD(RegData), .RD1(RD1), .RD2(MemData), .clk(clk),
    .reset(reset), .WE(RegWrite));
  // Probe on MemData
  // Probe on RD
  // Probe on RD
  // Probe on RD
  // Probe on Instr
  // Probe on RegData
  // Probe on MemData
  // Probe on RegAddr
  // Probe on MemAddr

  // Other names for the same wires on the sheet: funct[5:0] = Instr[5:0]; imm16[15:0] = Instr[15:0];
  //   J_address[25:0] = Instr[25:0]; shamt[4:0] = Instr[10:6]; rd_t[4:0] = Instr[15:11]; rt[4:0] = Instr[20:16];
  //   rs[4:0] = Instr[25:21]; opcode[5:0] = Instr[31:26]; RD2[31:0] = MemData; WE_DM = MemWrite; WE_grf = RegWrite

  // Notes on the sheet:
  //   CPU
  //   built by Charles
endmodule

module GRF (
  input  [4:0] A1,
  input  [4:0] A2,
  input  [4:0] A3,
  input  [31:0] WD,
  input  clk,
  input  reset,
  input  WE,
  output [31:0] RD1,
  output [31:0] RD2
);

  wire [31:0] in01, in02, in03, in04, in05, in06, in07, in08, in09, in10, in11, in12, in13, in14, in15, in16,
       in17, in18, in19, in20, in21, in22, in23, in24, in25, in26, in27, in28, in29, in30, in31, out00,
       out01, out02, out03, out04, out05, out06, out07, out08, out09, out10, out11, out12, out13, out14,
       out15, out16, out17, out18, out19, out20, out21, out22, out23, out24, out25, out26, out27, out28,
       out29, out30, out31;

  Demultiplexer #(.select(5), .width(32), .tristate("true"), .enable("false")) demultiplexer_1 (
    .out1(in01), .out2(in02), .out3(in03), .out4(in04), .out5(in05), .out6(in06), .out7(in07), .out8(in08),
    .out9(in09), .out10(in10), .out11(in11), .out12(in12), .out13(in13), .out14(in14), .out15(in15),
    .out16(in16), .out17(in17), .out18(in18), .out19(in19), .out20(in20), .out21(in21), .out22(in22),
    .out23(in23), .out24(in24), .out25(in25), .out26(in26), .out27(in27), .out28(in28), .out29(in29),
    .out30(in30), .out31(in31), .in(WD), .sel(A3));  // open: out0
  Register #(.width(32)) register_1 (.D({32{1'b0}}), .en(WE), .Q(out00), .clk(clk), .clr(reset));
  Register #(.width(32)) register_2 (.D(in04), .en(WE), .Q(out04), .clk(clk), .clr(reset));
  Register #(.width(32)) register_3 (.D(in08), .en(WE), .Q(out08), .clk(clk), .clr(reset));
  Register #(.width(32)) register_4 (.D(in12), .en(WE), .Q(out12), .clk(clk), .clr(reset));
  Register #(.width(32)) register_5 (.D(in16), .en(WE), .Q(out16), .clk(clk), .clr(reset));
  Register #(.width(32)) register_6 (.D(in20), .en(WE), .Q(out20), .clk(clk), .clr(reset));
  Register #(.width(32)) register_7 (.D(in24), .en(WE), .Q(out24), .clk(clk), .clr(reset));
  Register #(.width(32)) register_8 (.D(in28), .en(WE), .Q(out28), .clk(clk), .clr(reset));
  Register #(.width(32)) register_9 (.D(in01), .en(WE), .Q(out01), .clk(clk), .clr(reset));
  Register #(.width(32)) register_10 (.D(in05), .en(WE), .Q(out05), .clk(clk), .clr(reset));
  Register #(.width(32)) register_11 (.D(in09), .en(WE), .Q(out09), .clk(clk), .clr(reset));
  Register #(.width(32)) register_12 (.D(in13), .en(WE), .Q(out13), .clk(clk), .clr(reset));
  Register #(.width(32)) register_13 (.D(in17), .en(WE), .Q(out17), .clk(clk), .clr(reset));
  Register #(.width(32)) register_14 (.D(in21), .en(WE), .Q(out21), .clk(clk), .clr(reset));
  Register #(.width(32)) register_15 (.D(in25), .en(WE), .Q(out25), .clk(clk), .clr(reset));
  Register #(.width(32)) register_16 (.D(in29), .en(WE), .Q(out29), .clk(clk), .clr(reset));
  Register #(.width(32)) register_17 (.D(in02), .en(WE), .Q(out02), .clk(clk), .clr(reset));
  Register #(.width(32)) register_18 (.D(in06), .en(WE), .Q(out06), .clk(clk), .clr(reset));
  Register #(.width(32)) register_19 (.D(in10), .en(WE), .Q(out10), .clk(clk), .clr(reset));
  Register #(.width(32)) register_20 (.D(in14), .en(WE), .Q(out14), .clk(clk), .clr(reset));
  Register #(.width(32)) register_21 (.D(in18), .en(WE), .Q(out18), .clk(clk), .clr(reset));
  Register #(.width(32)) register_22 (.D(in22), .en(WE), .Q(out22), .clk(clk), .clr(reset));
  Register #(.width(32)) register_23 (.D(in26), .en(WE), .Q(out26), .clk(clk), .clr(reset));
  Register #(.width(32)) register_24 (.D(in30), .en(WE), .Q(out30), .clk(clk), .clr(reset));
  Register #(.width(32)) register_25 (.D(in07), .en(WE), .Q(out07), .clk(clk), .clr(reset));
  Register #(.width(32)) register_26 (.D(in03), .en(WE), .Q(out03), .clk(clk), .clr(reset));
  Register #(.width(32)) register_27 (.D(in11), .en(WE), .Q(out11), .clk(clk), .clr(reset));
  Register #(.width(32)) register_28 (.D(in15), .en(WE), .Q(out15), .clk(clk), .clr(reset));
  Register #(.width(32)) register_29 (.D(in19), .en(WE), .Q(out19), .clk(clk), .clr(reset));
  Register #(.width(32)) register_30 (.D(in23), .en(WE), .Q(out23), .clk(clk), .clr(reset));
  Register #(.width(32)) register_31 (.D(in27), .en(WE), .Q(out27), .clk(clk), .clr(reset));
  Register #(.width(32)) register_32 (.D(in31), .en(WE), .Q(out31), .clk(clk), .clr(reset));
  Multiplexer #(.select(5), .width(32), .enable("false")) multiplexer_1 (
    .in0(out00), .in1(out01), .in2(out02), .in3(out03), .in4(out04), .in5(out05), .in6(out06), .in7(out07),
    .in8(out08), .in9(out09), .in10(out10), .in11(out11), .in12(out12), .in13(out13), .in14(out14),
    .in15(out15), .in16(out16), .in17(out17), .in18(out18), .in19(out19), .in20(out20), .in21(out21),
    .in22(out22), .in23(out23), .in24(out24), .in25(out25), .in26(out26), .in27(out27), .in28(out28),
    .in29(out29), .in30(out30), .in31(out31), .out(RD1), .sel(A1));
  Multiplexer #(.select(5), .width(32), .enable("false")) multiplexer_2 (
    .in0(out00), .in1(out01), .in2(out02), .in3(out03), .in4(out04), .in5(out05), .in6(out06), .in7(out07),
    .in8(out08), .in9(out09), .in10(out10), .in11(out11), .in12(out12), .in13(out13), .in14(out14),
    .in15(out15), .in16(out16), .in17(out17), .in18(out18), .in19(out19), .in20(out20), .in21(out21),
    .in22(out22), .in23(out23), .in24(out24), .in25(out25), .in26(out26), .in27(out27), .in28(out28),
    .in29(out29), .in30(out30), .in31(out31), .out(RD2), .sel(A2));
endmodule

module ALU (
  input  [31:0] A,
  input  [31:0] B,
  input  [2:0] ALUop,
  input  [1:0] change,
  output change_2,
  output [31:0] res
);

  wire beq, blez, less, more;
  wire [4:0] bit_extender_1_out;
  wire [31:0] Des_Add, Des_And, Des_Or, Des_sll, Des_Sub;

  Adder #(.width(32)) adder_1 (.a(A), .b(B), .out(Des_Add));  // open: cin, cout
  Subtractor #(.width(32)) subtractor_1 (.a(A), .b(B), .out(Des_Sub));  // open: bin, bout
  assign Des_And = A & B;  // AND_Gate and_1, 32 bits wide
  assign Des_Or = A | B;  // OR_Gate or_1, 32 bits wide
  Shifter #(.width(32)) shifter_1 (.in(A), .\dist (bit_extender_1_out), .out(Des_sll));
  Bit_Extender #(.in_width(32), .out_width(5)) bit_extender_1 (.in(B), .out(bit_extender_1_out));
  Comparator #(.width(32), .mode("unsigned")) comparator_1 (.a(A), .b(B), .eq(beq));  // open: gt, lt
  Comparator #(.width(32)) comparator_2 (.a(A), .b(B), .lt(less));  // open: gt, eq
  Comparator #(.width(32)) comparator_3 (.a(A), .b(B), .gt(more));  // open: eq, lt
  or or_2 (blez, beq, less);
  Multiplexer #(.select(2)) multiplexer_1 (
    .in0(beq), .in1(less), .in2(blez), .out(change_2), .sel(change));  // open: in3, en
  Multiplexer #(.select(3), .width(32), .enable("false")) multiplexer_2 (
    .in0(Des_Add), .in1(Des_Sub), .in2(Des_And), .in3(Des_Or), .in4(Des_sll), .out(res), .sel(ALUop));  // open: in5, in6, in7

  // Other names for the same wires on the sheet: eq = beq; slt = less; Src_A[31:0] = A; Src_B[31:0] = B
endmodule

module DM (
  input  [1:0] low2,
  input  [1:0] DM_type,
  input  [4:0] Address,
  input  WE,
  input  clk,
  input  reset,
  input  [31:0] WD,
  output [31:0] RD
);

  wire bit0, bit1, bit2, bit3;
  wire [7:0] multiplexer_9_out, RD0, RD1, RD2, RD3;
  wire [15:0] multiplexer_10_out;
  wire [31:0] multiplexer_1_out, new_b, new_h, out_b, out_h;

  Decoder #(.select(2)) decoder_1 (.out0(bit0), .out1(bit1), .out2(bit2), .out3(bit3), .sel(low2));  // open: en
  Multiplexer #(.select(2), .width(32)) multiplexer_1 (
    .in0(WD), .in1(new_h), .in2(new_b), .out(multiplexer_1_out), .sel(DM_type));  // open: in3, en
  // Probe on WD
  Multiplexer #(.width(8)) multiplexer_2 (.in0(RD0), .in1(WD[7:0]), .out(new_b[7:0]), .sel(bit0));  // open: en
  Multiplexer #(.width(8)) multiplexer_3 (.in0(RD2), .in1(WD[7:0]), .out(new_b[23:16]), .sel(bit2));  // open: en
  RAM #(.addrWidth(5), .dataWidth(32), .bus("separate")) ram_1 (
    .addr(Address), .din(multiplexer_1_out), .data({RD3, RD2, RD1, RD0}), .str(WE), .clk(clk), .clr(reset));  // open: sel, ld
  // Probe on new_b
  // Probe on new_h
  Multiplexer #(.width(8)) multiplexer_4 (.in0(RD1), .in1(WD[7:0]), .out(new_b[15:8]), .sel(bit1));  // open: en
  Multiplexer #(.width(8)) multiplexer_5 (.in0(RD3), .in1(WD[7:0]), .out(new_b[31:24]), .sel(bit3));  // open: en
  Multiplexer #(.width(8)) multiplexer_6 (.in0(RD0), .in1(WD[7:0]), .out(new_h[7:0]), .sel(bit0));  // open: en
  Multiplexer #(.width(8)) multiplexer_7 (.in0(RD2), .in1(WD[7:0]), .out(new_h[23:16]), .sel(bit2));  // open: en
  Multiplexer #(.select(2), .width(32)) multiplexer_8 (
    .in0({RD3, RD2, RD1, RD0}), .in1(out_h), .in2(out_b), .out(RD), .sel(DM_type));  // open: in3, en
  Multiplexer #(.select(2), .width(8)) multiplexer_9 (
    .in0(RD0), .in1(RD1), .in2(RD2), .in3(RD3), .out(multiplexer_9_out), .sel(low2));  // open: en
  assign out_b = {{24{multiplexer_9_out[7]}}, multiplexer_9_out};  // Bit_Extender bit_extender_1
  assign out_h = {{16{multiplexer_10_out[15]}}, multiplexer_10_out};  // Bit_Extender bit_extender_2
  Multiplexer #(.width(16)) multiplexer_10 (
    .in0({RD1, RD0}), .in1({RD3, RD2}), .out(multiplexer_10_out), .sel(low2[1]));  // open: en
  Multiplexer #(.width(8)) multiplexer_11 (.in0(RD1), .in1(WD[15:8]), .out(new_h[15:8]), .sel(bit0));  // open: en
  Multiplexer #(.width(8)) multiplexer_12 (.in0(RD3), .in1(WD[15:8]), .out(new_h[31:24]), .sel(bit2));  // open: en

  // Other names for the same wires on the sheet: RD_t[31:0] = {RD3, RD2, RD1, RD0}; new_b0[7:0] = new_b[7:0];
  //   new_b1[7:0] = new_b[15:8]; new_b2[7:0] = new_b[23:16]; new_b3[7:0] = new_b[31:24]; new_h0[7:0] = new_h[7:0];
  //   new_h1[7:0] = new_h[15:8]; new_h2[7:0] = new_h[23:16]; new_h3[7:0] = new_h[31:24]; WD0[7:0] = WD[7:0];
  //   WD1[7:0] = WD[15:8]; WD2[7:0] = WD[23:16]; WD3[7:0] = WD[31:24]
endmodule

module EXT (
  input  [15:0] imm16,
  input  sign,
  output [31:0] imm32
);

  wire [15:0] signed16, unsigned16;
  wire [31:0] signed32, unsigned32;

  Demultiplexer #(.width(16), .enable("false")) demultiplexer_1 (
    .out0(unsigned16), .out1(signed16), .in(imm16), .sel(sign));
  assign unsigned32 = {{16{1'b0}}, unsigned16};  // Bit_Extender bit_extender_1
  assign signed32 = {{16{signed16[15]}}, signed16};  // Bit_Extender bit_extender_2
  Multiplexer #(.width(32), .enable("false")) multiplexer_1 (.in0(unsigned32), .in1(signed32), .out(imm32), .sel(sign));
endmodule

module IFU (
  input  [2:0] branch,
  input  change,
  input  clk,
  input  reset,
  input  [31:0] imm32,
  output [31:0] instr,
  output [31:0] PC
);

  wire [4:0] bit_extender_1_out;
  wire [31:0] adder_2_out, beq, NPC, or_1_out, PC_front4, register_1_q, shifter_1_out, shifter_2_out;

  Register #(.width(32)) register_1 (.D(NPC), .Q(register_1_q), .clk(clk), .clr(reset));  // open: en
  assign PC_front4 = register_1_q & 32'hf0000000;  // AND_Gate and_1, 32 bits wide
  Shifter #(.width(32)) shifter_1 (.in(imm32), .\dist (5'b00010), .out(shifter_1_out));
  assign or_1_out = shifter_1_out | PC_front4;  // OR_Gate or_1, 32 bits wide
  Shifter #(.width(32), .shift("lr")) shifter_2 (.in(register_1_q), .\dist (5'b00010), .out(shifter_2_out));
  Bit_Extender #(.in_width(32), .out_width(5)) bit_extender_1 (.in(shifter_2_out), .out(bit_extender_1_out));
  // Probe on bit_extender_1_out
  Adder #(.width(32)) adder_1 (.a(register_1_q), .b(32'h4), .out(PC));  // open: cin, cout
  Adder #(.width(32)) adder_2 (.a(PC), .b(shifter_1_out), .out(adder_2_out));  // open: cin, cout
  Multiplexer #(.width(32), .enable("false")) multiplexer_1 (.in0(PC), .in1(adder_2_out), .out(beq), .sel(change));
  IM im_1 (.Address(bit_extender_1_out), .Instr(instr));
  Multiplexer #(.select(3), .width(32), .enable("false")) multiplexer_2 (
    .in0(PC), .in1(beq), .in2(or_1_out), .in3(imm32), .out(NPC), .sel(branch));  // open: in4, in5, in6, in7

  // Other names for the same wires on the sheet: choose[2:0] = branch

  // Notes on the sheet:
  //   PC->PC+4
endmodule

module Controller (
  input  [5:0] op,
  input  [5:0] func,
  output [2:0] ALUop,
  output Wegrf,
  output WeDm,
  output [2:0] branch,
  output [1:0] AluSrc1,
  output [1:0] AluSrc2,
  output [2:0] WhichReg,
  output [1:0] RegDst,
  output SignExt,
  output [1:0] B_change,
  output [1:0] DM_type
);

  wire add, addi, addu, ALU_op, \and , andi, beq, bitfinder_3_found, bitfinder_6_found, blez, I, J, j_t, jal,
       jr, lb, lh, lui, lw, not_1_out, not_2_out, not_3_out, not_4_out, not_5_out, not_6_out, not_7_out,
       not_8_out, not_9_out, not_10_out, not_11_out, not_13_out, \or , ori, R, sb, sh, sll, sllv, slt, sub,
       subu, sw, zero, zero_n;
  wire [1:0] or_17_out, R_2_out;
  wire [1:1] or_12_out;
  wire [2:0] bitfinder_2_index, bitfinder_3_index, bitfinder_6_index, or_10_out, or_14_out;
  wire [2:1] or_7_out;
  wire [4:0] or_2_out;

  not not_1 (not_1_out, op[5]);
  not not_2 (not_2_out, op[1]);
  not not_3 (not_3_out, op[3]);
  not not_4 (not_4_out, op[4]);
  not not_5 (not_5_out, op[2]);
  not not_6 (not_6_out, func[5]);
  not not_7 (not_7_out, op[0]);
  Comparator #(.width(6)) comparator_1 (.a(op), .b({6{1'b0}}), .eq(zero));  // open: gt, lt
  not not_8 (not_8_out, func[4]);
  not not_9 (not_9_out, func[2]);
  not not_10 (not_10_out, func[1]);
  not not_11 (not_11_out, func[3]);
  not not_12 (zero_n, zero);
  not not_13 (not_13_out, func[0]);
  and u_addu (addu, zero, func[5], not_8_out, not_11_out, not_9_out, not_10_out, func[0]);
  and u_subu (subu, zero, func[5], not_8_out, not_11_out, not_9_out, func[1], func[0]);
  and u_ori (ori, zero_n, not_1_out, not_4_out, op[3], op[2], not_2_out, op[0]);
  and u_lw (lw, zero_n, op[5], not_4_out, not_3_out, not_5_out, op[1], op[0]);
  and u_sw (sw, zero_n, op[5], not_4_out, op[3], not_5_out, op[1], op[0]);
  and u_beq (beq, zero_n, not_1_out, not_4_out, not_3_out, op[2], not_2_out, not_7_out);
  and u_lui (lui, zero_n, not_1_out, not_4_out, op[3], op[2], op[1], op[0]);
  and u_andi (andi, zero_n, not_1_out, not_4_out, op[3], op[2], not_2_out, not_7_out);
  and u_jal (jal, zero_n, not_1_out, not_4_out, not_3_out, not_5_out, op[1], op[0]);
  and u_j (j_t, zero_n, not_1_out, not_4_out, not_3_out, not_5_out, op[1], not_7_out);
  and u_jr (jr, zero, not_6_out, not_8_out, func[3], not_9_out, not_10_out, not_13_out);
  and u_sll (sll, zero, not_6_out, not_8_out, not_11_out, not_9_out, not_10_out, not_13_out);
  and u_add (add, zero, func[5], not_8_out, not_11_out, not_9_out, not_10_out, not_13_out);
  and u_sub (sub, zero, func[5], not_8_out, not_11_out, not_9_out, func[1], not_13_out);
  and u_slt (slt, zero, func[5], not_8_out, func[3], not_9_out, func[1], not_13_out);
  and u_lb (lb, zero_n, op[5], not_4_out, not_3_out, not_5_out, not_2_out, not_7_out);
  and u_sb (sb, zero_n, op[5], not_4_out, op[3], not_5_out, not_2_out, not_7_out);
  and u_lh (lh, zero_n, op[5], not_4_out, not_3_out, not_5_out, not_2_out, op[0]);
  and u_sh (sh, zero_n, op[5], not_4_out, op[3], not_5_out, not_2_out, op[0]);
  and u_addi (addi, zero_n, not_1_out, not_4_out, op[3], not_5_out, not_2_out, not_7_out);
  and u_and (\and , zero, func[5], not_8_out, not_11_out, func[2], not_10_out, not_13_out);
  and u_or (\or , zero, func[5], not_8_out, not_11_out, func[2], not_10_out, func[0]);
  and u_sllv (sllv, zero, not_6_out, not_8_out, not_11_out, func[2], not_10_out, not_13_out);
  and u_blez (blez, zero_n, not_1_out, not_4_out, not_3_out, not_5_out, not_2_out, op[0]);
  or u_R (R, addu, subu, add, sub, \and , \or );
  or or_2 (or_2_out[0], addu, addi, add);
  or or_3 (or_2_out[1], subu, sub);
  or or_4 (or_2_out[2], andi, \and );
  or or_5 (or_2_out[3], ori, \or );
  or or_6 (or_2_out[4], sll, sllv);
  or or_7 (or_7_out[1], beq, blez);
  or or_8 (or_7_out[2], j_t, jal);
  or or_9 (or_17_out[1], 1'b0, sll);
  or or_10 (or_10_out[0], R, sllv, beq);
  or or_11 (or_10_out[2], 1'b0, sll);
  or or_12 (or_12_out[1], lb, lw, lh);
  or or_13 (R_2_out[1], beq, I, lui, addi);
  or or_14 (or_14_out[0], lw, sw);
  or or_15 (or_14_out[1], lh, sh);
  or or_16 (or_14_out[2], lb, sb);
  or or_17 (or_17_out[0], \or , \and , addu, subu, beq, I, add, sub, sllv, blez);
  or R_2 (R_2_out[0], \and , \or , addu, subu, add, sub);
  or or_18 (SignExt, sh, lh, lb, lw, sw, beq, andi, sb, addi, blez);
  BitFinder #(.width(4)) bitfinder_1 (.in({1'b0, blez, slt, beq}), .index(B_change));  // open: found
  or u_I (I, sb, lw, sw, addi, ori, andi, lb, lh, sh);
  BitFinder #(.width(7)) bitfinder_2 (.in({2'b00, or_2_out}), .index(bitfinder_2_index), .found(ALU_op));
  or or_19 (Wegrf, \or , \and , lb, sub, addu, subu, ori, lui, sll, jal, 1'b0, lw, add, slt, addi, sllv, lh);
  or or_20 (WeDm, sw, sb, sh);
  BitFinder bitfinder_3 (.in({4'b0000, jr, or_7_out, 1'b0}), .index(bitfinder_3_index), .found(bitfinder_3_found));
  BitFinder #(.width(4)) bitfinder_4 (.in({2'b00, or_17_out}), .index(AluSrc1));  // open: found
  BitFinder #(.width(4)) bitfinder_5 (.in({blez, or_10_out[2], I, or_10_out[0]}), .index(AluSrc2));  // open: found
  BitFinder bitfinder_6 (
    .in({3'b000, slt, jal, lui, or_12_out[1], ALU_op}), .index(bitfinder_6_index), .found(bitfinder_6_found));
  Multiplexer #(.width(3), .enable("false")) multiplexer_1 (
    .in0(3'b000), .in1(bitfinder_2_index), .out(ALUop), .sel(ALU_op));
  Multiplexer #(.width(3), .enable("false")) multiplexer_2 (
    .in0(3'b000), .in1(bitfinder_6_index), .out(WhichReg), .sel(bitfinder_6_found));
  BitFinder #(.width(4)) bitfinder_7 (.in({1'b0, jal, R_2_out}), .index(RegDst));  // open: found
  BitFinder #(.width(4)) bitfinder_8 (.in({1'b0, or_14_out}), .index(DM_type));  // open: found
  or J_2 (J, jal, j_t, jr);
  Multiplexer #(.width(3), .enable("false")) multiplexer_3 (
    .in0(3'b000), .in1(bitfinder_3_index), .out(branch), .sel(bitfinder_3_found));

  // Other names for the same wires on the sheet: funct[5:0] = func; opcode[5:0] = op
endmodule

module IM (
  input  [4:0] Address,
  output [31:0] Instr
);

  ROM #(.addrWidth(5), .dataWidth(32)) rom_1 (.addr(Address), .data(Instr));  // open: sel

  // Notes on the sheet:
  //   contents of rom_1 (hex, n*v repeats v):
  //   35080008 35290009 354a000a 356b000b 840c0 a3a80000 a3a90001 a3aa0002 a3ab0003 8fa80000 87a80000
endmodule
