// Logisim project Binary conversion.circ as structural Verilog: 2 circuits, main circuit conversion
module conversion (
  input  [8:0] in,
  input  [1:0] op,
  output [3:0] out_3,
  output [3:0] out_4,
  output [3:0] out_5
);

  wire [4:0] multiplexer_1_out;
  wire [19:0] bit_extender_1_out;

  assign bit_extender_1_out = {{11{1'b0}}, in};  // Bit_Extender bit_extender_1
  Multiplexer #(.select(2), .width(5), .enable("false")) multiplexer_1 (
    .in0(5'b01000), .in1(5'b01010), .in2(5'b10000), .out(multiplexer_1_out), .sel(op));  // open: in3
  change change_1 (.in_1(bit_extender_1_out), .op(multiplexer_1_out), .out1(out_5), .out2(out_4), .out3(out_3));
endmodule

module change (
  input  [19:0] in_1,
  input  [4:0] op,
  output [3:0] out1,
  output [3:0] out2,
  output [3:0] out3
);

  wire [4:0] divider_2_out, divider_2_rem;
  wire [9:0] div, divider_1_out, divider_1_rem;

  assign div = {{5{1'b0}}, op};  // Bit_Extender bit_extender_1
  Divider #(.width(10)) divider_1 (
    .a(in_1[9:0]), .b(div), .out(divider_1_out), .upper(in_1[19:10]), .rem(divider_1_rem));
  Divider #(.width(5)) divider_2 (
    .a(divider_1_out[4:0]), .b(op), .out(divider_2_out), .upper(divider_1_out[9:5]), .rem(divider_2_rem));
  Bit_Extender #(.in_width(10), .out_width(4)) bit_extender_2 (.in(divider_1_rem), .out(out3));
  Bit_Extender #(.in_width(5), .out_width(4)) bit_extender_3 (.in(divider_2_out), .out(out1));
  Bit_Extender #(.in_width(5), .out_width(4)) bit_extender_4 (.in(divider_2_rem), .out(out2));

  // Other names for the same wires on the sheet: div2[4:0] = op
endmodule
