// Logisim project bus.circ as structural Verilog: 2 circuits, main circuit main
module main (
  input  in_1,
  input  [1:0] in_2,
  input  in_3,
  output [1:0] out_4
);

  wire clk, comparator_1_eq;
  wire [1:0] change_1_out_3, multiplexer_1_out;
  wire [7:0] counter_1_q;

  Clock clock_1 (.out(clk));
  Counter #(.ongoal("stay")) counter_1 (.Q(counter_1_q), .clk(clk), .clr(in_3));  // open: load, D, count, carry
  Multiplexer #(.width(2)) multiplexer_1 (
    .in0(out_4), .in1(in_2), .out(multiplexer_1_out), .sel(comparator_1_eq));  // open: en
  Comparator comparator_1 (.a({8{1'b0}}), .b(counter_1_q), .eq(comparator_1_eq));  // open: gt, lt
  change change_1 (.\input (in_1), .in_2(multiplexer_1_out), .out_3(change_1_out_3));
  Register #(.width(2)) register_1 (.D(change_1_out_3), .Q(out_4), .clk(clk));  // open: en, clr

  // Other names for the same wires on the sheet: out[1:0] = out_4
endmodule

module change (
  input  \input ,
  input  [1:0] in_2,
  output [1:0] out_3
);

  wire and_1_out, and_2_out, and_3_out, and_4_out, not_1_out, not_2_out, not_3_out, not_4_out, not_5_out;

  not not_1 (not_1_out, in_2[0]);
  not not_2 (not_2_out, in_2[1]);
  not not_3 (not_3_out, in_2[0]);
  not not_4 (not_4_out, in_2[0]);
  not not_5 (not_5_out, in_2[1]);
  and and_1 (and_1_out, \input , not_1_out);
  and and_2 (and_2_out, not_2_out, not_3_out);
  and and_3 (and_3_out, in_2[1], in_2[0]);
  and and_4 (and_4_out, \input , not_4_out);
  or or_1 (out_3[1], not_5_out, and_1_out);
  or or_2 (out_3[0], and_2_out, and_3_out, and_4_out);
endmodule
