// Logisim project calc_mark.circ as structural Verilog: 1 circuit, main circuit main
module main (
  input  [2:0] tea,
  input  [1:0] s1,
  input  [1:0] s2,
  output [3:0] total
);

  wire choose, comparator_1_eq;
  wire [3:0] adder_1_out, adder_2_out, bit_extender_1_out, bit_extender_2_out, bit_extender_3_out;

  assign bit_extender_1_out = {{2{1'b0}}, s1};  // Bit_Extender bit_extender_1
  assign bit_extender_2_out = {{2{1'b0}}, s2};  // Bit_Extender bit_extender_2
  not not_1 (choose, comparator_1_eq);
  Comparator #(.width(3)) comparator_1 (.a(tea), .b(3'b000), .eq(comparator_1_eq));  // open: gt, lt
  assign bit_extender_3_out = {{1{1'b0}}, tea};  // Bit_Extender bit_extender_3
  Adder #(.width(4)) adder_1 (.a(bit_extender_1_out), .b(bit_extender_2_out), .out(adder_1_out));  // open: cin, cout
  Adder #(.width(4)) adder_2 (.a(bit_extender_3_out), .b(adder_1_out), .out(adder_2_out));  // open: cin, cout
  Multiplexer #(.width(4)) multiplexer_1 (.in0(4'b0000), .in1(adder_2_out), .out(total), .sel(choose));  // open: en
endmodule
